// Logisim project 32-np-nc.circ as structural Verilog: 14 circuits, main circuit main
module main (
  input  [31:0] Instruction,
  input  Clock,
  input  RESET,
  output [31:0] x0,
  output [31:0] x1,
  output [31:0] x2,
  output [31:0] x3,
  output [31:0] x4,
  output [31:0] x5,
  output [31:0] x6,
  output [31:0] x7,
  output [31:0] x8,
  output [31:0] x9,
  output [31:0] x10,
  output [31:0] x11,
  output [31:0] x12,
  output [31:0] x13,
  output [31:0] x14,
  output [31:0] x15,
  output [31:0] x16,
  output [31:0] x17,
  output [31:0] x18,
  output [31:0] x19,
  output [31:0] x20,
  output [31:0] x21,
  output [31:0] x22,
  output [31:0] x23,
  output [31:0] x24,
  output [31:0] x25,
  output [31:0] x26,
  output [31:0] x27,
  output [31:0] x28,
  output [31:0] x29,
  output End,
  output Error,
  output [31:0] x30,
  output [31:0] x31,
  output [31:0] PC
);

  wire ALU_In_1, ALU_In_2, BComp_U, Eq, LT, Next_PC_Sel, RAM_Read_U, RAM_WEn, Reg_WEn;
  wire [1:0] RAM_num, WB_Sel;
  wire [2:0] Imm_Enc;
  wire [3:0] ALU_Op;
  wire [31:0] adder_1_out, ALU, Imm, multiplexer_1_out, multiplexer_2_out, RAM_Out, rs1, rs2, WB_Data;

  PC pc_1 (.clk(Clock), .PC_Out(PC), .clear(RESET), .ALU_Out(ALU), .Next_PC_Sel(Next_PC_Sel));
  Imm_Decoder imm_decoder_1 (.Imm_Bits(Instruction[31:7]), .Immediate(Imm), .Imm_Encoding(Imm_Enc));
  Control control_1 (
    .Instr(Instruction), .Imm_Enc(Imm_Enc), .BComp_U(BComp_U), .ALU_In_1(ALU_In_1), .ALU_In_2(ALU_In_2),
    .ALU_Op(ALU_Op), .RAM_WEn(RAM_WEn), .WB_Sel(WB_Sel), .Reg_WEn(Reg_WEn), .Next_PC_Sel(Next_PC_Sel),
    .RAM_Read_U(RAM_Read_U), .Continue_Execution(End), .Valid_Instr(Error), .RAM_num(RAM_num), .LT(LT),
    .Eq(Eq));
  Regs regs_1 (
    .Write_Data(WB_Data), .clk(Clock), .RESET(RESET), .Reg1(Instruction[19:15]), .Reg2(Instruction[24:20]),
    .Wr_Reg(Instruction[11:7]), .wen(Reg_WEn), .Reg1_Data(rs1), .Reg2_Data(rs2), .x0(x0), .x1(x1), .x2(x2),
    .x3(x3), .x4(x4), .x5(x5), .x6(x6), .x7(x7), .x16(x16), .x17(x17), .x18(x18), .x19(x19), .x20(x20),
    .x21(x21), .x22(x22), .x23(x23), .x8(x8), .x9(x9), .x10(x10), .x11(x11), .x12(x12), .x13(x13), .x14(x14),
    .x15(x15), .x24(x24), .x25(x25), .x26(x26), .x27(x27), .x28(x28), .x29(x29), .x30(x30), .x31(x31));
  Branch_Comp branch_comp_1 (.rs1(rs1), .Unsign(BComp_U), .rs2(rs2), .Eq(Eq), .LT(LT));
  Multiplexer #(.width(32), .enable("false")) multiplexer_1 (
    .in0(rs1), .in1(PC), .out(multiplexer_1_out), .sel(ALU_In_1));
  Multiplexer #(.width(32), .enable("false")) multiplexer_2 (
    .in0(rs2), .in1(Imm), .out(multiplexer_2_out), .sel(ALU_In_2));
  ALU alu_1 (.In_1(multiplexer_1_out), .In_2(multiplexer_2_out), .Out(ALU), .Op(ALU_Op));
  RAM ram_1 (
    .ALU(ALU), .Write_Data(rs2), .clk(Clock), .clr(RESET), .Wr_En(RAM_WEn), .Read_Unsigned(RAM_Read_U),
    .RAM_Out(RAM_Out), .RAM_num(RAM_num));
  Adder #(.width(32)) adder_1 (.a(32'h4), .b(PC), .out(adder_1_out));  // open: cin, cout
  Multiplexer #(.select(2), .width(32), .enable("false")) multiplexer_3 (
    .in0(adder_1_out), .in1(ALU), .in2(RAM_Out), .in3(32'hbad), .out(WB_Data), .sel(WB_Sel));

  // Other names for the same wires on the sheet: clk = Clock; Instr[31:0] = Instruction; Invalid_Instr = Error;
  //   Stop_Exec = End; x0_Data[31:0] = x0; x1_Data[31:0] = x1; x2_Data[31:0] = x2; x3_Data[31:0] = x3;
  //   x4_Data[31:0] = x4; x5_Data[31:0] = x5; x6_Data[31:0] = x6; x7_Data[31:0] = x7; x8_Data[31:0] = x8;
  //   x9_Data[31:0] = x9; x10_Data[31:0] = x10; x11_Data[31:0] = x11; x12_Data[31:0] = x12; x13_Data[31:0] = x13;
  //   x14_Data[31:0] = x14; x15_Data[31:0] = x15; x16_Data[31:0] = x16; x17_Data[31:0] = x17; x18_Data[31:0] = x18;
  //   x19_Data[31:0] = x19; x20_Data[31:0] = x20; x21_Data[31:0] = x21; x22_Data[31:0] = x22; x23_Data[31:0] = x23;
  //   x24_Data[31:0] = x24; x25_Data[31:0] = x25; x26_Data[31:0] = x26; x27_Data[31:0] = x27; x28_Data[31:0] = x28;
  //   x29_Data[31:0] = x29; x30_Data[31:0] = x30; x31_Data[31:0] = x31

  // Notes on the sheet:
  //   Execution Control
  //   ALU Control
  //   RAM Control
  //   Regfile Control
endmodule

module PC (
  input  [31:0] ALU_Out,
  input  Next_PC_Sel,
  input  clk,
  input  clear,
  output [31:0] PC_Out
);

  wire [31:0] multiplexer_1_out, PC___4;

  Multiplexer #(.width(32), .enable("false")) multiplexer_1 (
    .in0(PC___4), .in1(ALU_Out), .out(multiplexer_1_out), .sel(Next_PC_Sel));
  Register #(.width(32)) PC (.D(multiplexer_1_out), .Q(PC_Out), .clk(clk), .clr(clear));  // open: en
  Adder #(.width(32)) adder_1 (.a(32'h4), .b(PC_Out), .out(PC___4));  // open: cin, cout
endmodule

module Regs (
  input  [31:0] Write_Data,
  input  clk,
  input  RESET,
  input  [4:0] Reg1,
  input  [4:0] Reg2,
  input  wen,
  input  [4:0] Wr_Reg,
  output [31:0] x0,
  output [31:0] x1,
  output [31:0] x2,
  output [31:0] x3,
  output [31:0] x4,
  output [31:0] x5,
  output [31:0] x6,
  output [31:0] x7,
  output [31:0] x8,
  output [31:0] x9,
  output [31:0] x10,
  output [31:0] x11,
  output [31:0] x12,
  output [31:0] x13,
  output [31:0] x14,
  output [31:0] x15,
  output [31:0] x16,
  output [31:0] x17,
  output [31:0] x18,
  output [31:0] x19,
  output [31:0] x20,
  output [31:0] x21,
  output [31:0] x22,
  output [31:0] x23,
  output [31:0] x24,
  output [31:0] x25,
  output [31:0] x26,
  output [31:0] x27,
  output [31:0] x28,
  output [31:0] x29,
  output [31:0] x30,
  output [31:0] x31,
  output [31:0] Reg1_Data,
  output [31:0] Reg2_Data
);

  wire demultiplexer_1_out0, x1_WEn, x2_WEn, x3_WEn, x4_WEn, x5_WEn, x6_WEn, x7_WEn, x8_WEn, x9_WEn, x10_WEn,
       x11_WEn, x12_WEn, x13_WEn, x14_WEn, x15_WEn, x16_WEn, x17_WEn, x18_WEn, x19_WEn, x20_WEn, x21_WEn,
       x22_WEn, x23_WEn, x24_WEn, x25_WEn, x26_WEn, x27_WEn, x28_WEn, x29_WEn, x30_WEn, x31_WEn;

  LED Write_to_x0 (.in(demultiplexer_1_out0));
  Demultiplexer #(.select(5), .disabled(0), .enable("false")) demultiplexer_1 (
    .out0(demultiplexer_1_out0), .out1(x1_WEn), .out2(x2_WEn), .out3(x3_WEn), .out4(x4_WEn), .out5(x5_WEn),
    .out6(x6_WEn), .out7(x7_WEn), .out8(x8_WEn), .out9(x9_WEn), .out10(x10_WEn), .out11(x11_WEn),
    .out12(x12_WEn), .out13(x13_WEn), .out14(x14_WEn), .out15(x15_WEn), .out16(x16_WEn), .out17(x17_WEn),
    .out18(x18_WEn), .out19(x19_WEn), .out20(x20_WEn), .out21(x21_WEn), .out22(x22_WEn), .out23(x23_WEn),
    .out24(x24_WEn), .out25(x25_WEn), .out26(x26_WEn), .out27(x27_WEn), .out28(x28_WEn), .out29(x29_WEn),
    .out30(x30_WEn), .out31(x31_WEn), .in(wen), .sel(Wr_Reg));
  Register #(.width(32)) u_x4 (.D(Write_Data), .en(x4_WEn), .Q(x4), .clk(clk), .clr(RESET));
  Register #(.width(32)) u_x8 (.D(Write_Data), .en(x8_WEn), .Q(x8), .clk(clk), .clr(RESET));
  Register #(.width(32)) u_x12 (.D(Write_Data), .en(x12_WEn), .Q(x12), .clk(clk), .clr(RESET));
  Register #(.width(32)) u_x16 (.D(Write_Data), .en(x16_WEn), .Q(x16), .clk(clk), .clr(RESET));
  Register #(.width(32)) u_x20 (.D(Write_Data), .en(x20_WEn), .Q(x20), .clk(clk), .clr(RESET));
  Register #(.width(32)) u_x24 (.D(Write_Data), .en(x24_WEn), .Q(x24), .clk(clk), .clr(RESET));
  Register #(.width(32)) u_x28 (.D(Write_Data), .en(x28_WEn), .Q(x28), .clk(clk), .clr(RESET));
  Register #(.width(32)) u_x1 (.D(Write_Data), .en(x1_WEn), .Q(x1), .clk(clk), .clr(RESET));
  Register #(.width(32)) u_x5 (.D(Write_Data), .en(x5_WEn), .Q(x5), .clk(clk), .clr(RESET));
  Register #(.width(32)) u_x9 (.D(Write_Data), .en(x9_WEn), .Q(x9), .clk(clk), .clr(RESET));
  Register #(.width(32)) u_x13 (.D(Write_Data), .en(x13_WEn), .Q(x13), .clk(clk), .clr(RESET));
  Register #(.width(32)) u_x17 (.D(Write_Data), .en(x17_WEn), .Q(x17), .clk(clk), .clr(RESET));
  Register #(.width(32)) u_x21 (.D(Write_Data), .en(x21_WEn), .Q(x21), .clk(clk), .clr(RESET));
  Register #(.width(32)) u_x25 (.D(Write_Data), .en(x25_WEn), .Q(x25), .clk(clk), .clr(RESET));
  Register #(.width(32)) u_x29 (.D(Write_Data), .en(x29_WEn), .Q(x29), .clk(clk), .clr(RESET));
  Register #(.width(32)) u_x2 (.D(Write_Data), .en(x2_WEn), .Q(x2), .clk(clk), .clr(RESET));
  Register #(.width(32)) u_x6 (.D(Write_Data), .en(x6_WEn), .Q(x6), .clk(clk), .clr(RESET));
  Register #(.width(32)) u_x10 (.D(Write_Data), .en(x10_WEn), .Q(x10), .clk(clk), .clr(RESET));
  Register #(.width(32)) u_x14 (.D(Write_Data), .en(x14_WEn), .Q(x14), .clk(clk), .clr(RESET));
  Register #(.width(32)) u_x18 (.D(Write_Data), .en(x18_WEn), .Q(x18), .clk(clk), .clr(RESET));
  Register #(.width(32)) u_x22 (.D(Write_Data), .en(x22_WEn), .Q(x22), .clk(clk), .clr(RESET));
  Register #(.width(32)) u_x26 (.D(Write_Data), .en(x26_WEn), .Q(x26), .clk(clk), .clr(RESET));
  Register #(.width(32)) u_x30 (.D(Write_Data), .en(x30_WEn), .Q(x30), .clk(clk), .clr(RESET));
  Register #(.width(32)) u_x3 (.D(Write_Data), .en(x3_WEn), .Q(x3), .clk(clk), .clr(RESET));
  Register #(.width(32)) u_x7 (.D(Write_Data), .en(x7_WEn), .Q(x7), .clk(clk), .clr(RESET));
  Register #(.width(32)) u_x11 (.D(Write_Data), .en(x11_WEn), .Q(x11), .clk(clk), .clr(RESET));
  Register #(.width(32)) u_x15 (.D(Write_Data), .en(x15_WEn), .Q(x15), .clk(clk), .clr(RESET));
  Register #(.width(32)) u_x19 (.D(Write_Data), .en(x19_WEn), .Q(x19), .clk(clk), .clr(RESET));
  Register #(.width(32)) u_x23 (.D(Write_Data), .en(x23_WEn), .Q(x23), .clk(clk), .clr(RESET));
  Register #(.width(32)) u_x27 (.D(Write_Data), .en(x27_WEn), .Q(x27), .clk(clk), .clr(RESET));
  Register #(.width(32)) u_x31 (.D(Write_Data), .en(x31_WEn), .Q(x31), .clk(clk), .clr(RESET));
  Multiplexer #(.select(5), .width(32), .enable("false")) multiplexer_1 (
    .in0({32{1'b0}}), .in1(x1), .in2(x2), .in3(x3), .in4(x4), .in5(x5), .in6(x6), .in7(x7), .in8(x8),
    .in9(x9), .in10(x10), .in11(x11), .in12(x12), .in13(x13), .in14(x14), .in15(x15), .in16(x16), .in17(x17),
    .in18(x18), .in19(x19), .in20(x20), .in21(x21), .in22(x22), .in23(x23), .in24(x24), .in25(x25),
    .in26(x26), .in27(x27), .in28(x28), .in29(x29), .in30(x30), .in31(x31), .out(Reg1_Data), .sel(Reg1));
  Multiplexer #(.select(5), .width(32), .enable("false")) multiplexer_2 (
    .in0({32{1'b0}}), .in1(x1), .in2(x2), .in3(x3), .in4(x4), .in5(x5), .in6(x6), .in7(x7), .in8(x8),
    .in9(x9), .in10(x10), .in11(x11), .in12(x12), .in13(x13), .in14(x14), .in15(x15), .in16(x16), .in17(x17),
    .in18(x18), .in19(x19), .in20(x20), .in21(x21), .in22(x22), .in23(x23), .in24(x24), .in25(x25),
    .in26(x26), .in27(x27), .in28(x28), .in29(x29), .in30(x30), .in31(x31), .out(Reg2_Data), .sel(Reg2));

  assign x0 = {32{1'b0}};

  // Other names for the same wires on the sheet: RES = RESET; WD[31:0] = Write_Data; x1_Data[31:0] = x1;
  //   x2_Data[31:0] = x2; x3_Data[31:0] = x3; x4_Data[31:0] = x4; x5_Data[31:0] = x5; x6_Data[31:0] = x6;
  //   x7_Data[31:0] = x7; x8_Data[31:0] = x8; x9_Data[31:0] = x9; x10_Data[31:0] = x10; x11_Data[31:0] = x11;
  //   x12_Data[31:0] = x12; x13_Data[31:0] = x13; x14_Data[31:0] = x14; x15_Data[31:0] = x15; x16_Data[31:0] = x16;
  //   x17_Data[31:0] = x17; x18_Data[31:0] = x18; x19_Data[31:0] = x19; x20_Data[31:0] = x20; x21_Data[31:0] = x21;
  //   x22_Data[31:0] = x22; x23_Data[31:0] = x23; x24_Data[31:0] = x24; x25_Data[31:0] = x25; x26_Data[31:0] = x26;
  //   x27_Data[31:0] = x27; x28_Data[31:0] = x28; x29_Data[31:0] = x29; x30_Data[31:0] = x30; x31_Data[31:0] = x31

  // Notes on the sheet:
  //   x0
endmodule

module Imm_Decoder (
  input  [24:0] Imm_Bits,
  input  [2:0] Imm_Encoding,
  output [31:0] Immediate
);

  wire [31:0] bit_extender_1_out, I, S, SB, U, UJ;

  assign bit_extender_1_out = {{12{Imm_Bits[24]}}, Imm_Bits[24:5]};  // Bit_Extender bit_extender_1
  assign I = {{20{Imm_Bits[24]}}, Imm_Bits[24:13]};  // Bit_Extender bit_extender_2
  assign S = {{20{Imm_Bits[24]}}, {Imm_Bits[24:18], Imm_Bits[4:0]}};  // Bit_Extender bit_extender_3
  assign SB = {{19{Imm_Bits[24]}}, {Imm_Bits[24], Imm_Bits[0], Imm_Bits[23:18], Imm_Bits[4:1], 1'b0}};  // Bit_Extender bit_extender_4
  Shifter #(.width(32)) shifter_1 (.in(bit_extender_1_out), .\dist (5'b01100), .out(U));
  assign UJ = {{11{Imm_Bits[24]}}, {Imm_Bits[24], Imm_Bits[12:5], Imm_Bits[13], Imm_Bits[23:14], 1'b0}};  // Bit_Extender bit_extender_5
  Multiplexer #(.select(3), .width(32), .disabled(0), .enable("false")) multiplexer_1 (
    .in0(I), .in1(S), .in2(SB), .in3(UJ), .in4(U), .in5(32'hbad), .in6(32'hbad), .in7(32'hbad),
    .out(Immediate), .sel(Imm_Encoding));

  // Other names for the same wires on the sheet: Enc[2:0] = Imm_Encoding
endmodule

module ALU (
  input  [31:0] In_1,
  input  [31:0] In_2,
  input  [3:0] Op,
  output [31:0] Out
);

  wire comparator_1_lt, comparator_2_lt;
  wire [31:0] add, \and , div, mul, mulh, \or , rem, sll, slt, sltu, sra, srl, sub, \xor ;

  Adder #(.width(32)) adder_1 (.a(In_1), .b(In_2), .out(add));  // open: cin, cout
  Subtractor #(.width(32)) subtractor_1 (.a(In_1), .b(In_2), .out(sub));  // open: bin, bout
  Multiplier #(.width(32)) multiplier_1 (.a(In_1), .b(In_2), .out(mul), .cout(mulh));  // open: cin
  Divider #(.width(32)) divider_1 (.a(In_1), .b(In_2), .out(div), .rem(rem));  // open: upper
  Shifter #(.width(32)) shifter_1 (.in(In_1), .\dist (In_2[4:0]), .out(sll));
  Shifter #(.width(32), .shift("lr")) shifter_2 (.in(In_1), .\dist (In_2[4:0]), .out(srl));
  Shifter #(.width(32), .shift("ar")) shifter_3 (.in(In_1), .\dist (In_2[4:0]), .out(sra));
  Comparator #(.width(32)) comparator_1 (.a(In_1), .b(In_2), .lt(comparator_1_lt));  // open: gt, eq
  Comparator #(.width(32), .mode("unsigned")) comparator_2 (.a(In_1), .b(In_2), .lt(comparator_2_lt));  // open: gt, eq
  assign \or  = In_1 | In_2;  // OR_Gate or_1, 32 bits wide
  assign \and  = In_1 & In_2;  // AND_Gate and_1, 32 bits wide
  assign \xor  = In_1 ^ In_2;  // XOR_Gate xor_1, 32 bits wide
  assign slt = {{31{1'b0}}, comparator_1_lt};  // Bit_Extender bit_extender_1
  assign sltu = {{31{1'b0}}, comparator_2_lt};  // Bit_Extender bit_extender_2
  Multiplexer #(.select(4), .width(32), .enable("false")) multiplexer_1 (
    .in0(add), .in1(sub), .in2(mul), .in3(mulh), .in4(div), .in5(rem), .in6(sll), .in7(srl), .in8(sra),
    .in9(slt), .in10(sltu), .in11(\or ), .in12(\and ), .in13(\xor ), .in14(In_2), .in15(32'hbad), .out(Out),
    .sel(Op));
endmodule

module Branch_Comp (
  input  [31:0] rs1,
  input  Unsign,
  input  [31:0] rs2,
  output Eq,
  output LT
);

  wire SEq, SLT, UEq, ULT;

  Comparator #(.width(32)) comparator_1 (.a(rs1), .b(rs2), .eq(SEq), .lt(SLT));  // open: gt
  Comparator #(.width(32), .mode("unsigned")) comparator_2 (.a(rs1), .b(rs2), .eq(UEq), .lt(ULT));  // open: gt
  Multiplexer #(.enable("false")) multiplexer_1 (.in0(SEq), .in1(UEq), .out(Eq), .sel(Unsign));
  Multiplexer #(.enable("false")) multiplexer_2 (.in0(SLT), .in1(ULT), .out(LT), .sel(Unsign));
endmodule

module Control (
  input  [31:0] Instr,
  input  LT,
  input  Eq,
  output Valid_Instr,
  output Continue_Execution,
  output [2:0] Imm_Enc,
  output BComp_U,
  output ALU_In_1,
  output ALU_In_2,
  output [3:0] ALU_Op,
  output [1:0] RAM_num,
  output RAM_WEn,
  output RAM_Read_U,
  output [1:0] WB_Sel,
  output Reg_WEn,
  output Next_PC_Sel
);

  wire multiplexer_1_out, Next_PC_Cond, Next_PC_Uncond, not_1_out, not_2_out;
  wire [1:0] BComp;

  // Probe on {Instr[6:0], Instr[14:12], Instr[30], Instr[25]}
  ROM #(.addrWidth(12), .dataWidth(23)) rom_1 (
    .addr({Instr[6:0], Instr[14:12], Instr[30], Instr[25]}),
    .data({Valid_Instr, Continue_Execution, Imm_Enc, BComp_U, BComp, Next_PC_Uncond, Next_PC_Cond, ALU_In_1, ALU_In_2, ALU_Op, RAM_num, RAM_WEn, RAM_Read_U, WB_Sel, Reg_WEn}));  // open: sel
  not not_1 (not_1_out, LT);
  not not_2 (not_2_out, Eq);
  Multiplexer #(.select(2), .enable("false")) multiplexer_1 (
    .in0(LT), .in1(not_1_out), .in2(Eq), .in3(not_2_out), .out(multiplexer_1_out), .sel(BComp));
  Multiplexer #(.enable("false")) multiplexer_2 (
    .in0(Next_PC_Uncond), .in1(multiplexer_1_out), .out(Next_PC_Sel), .sel(Next_PC_Cond));

  // Other names for the same wires on the sheet: Reg_Wr_En = Reg_WEn; RAM_Wr_En = RAM_WEn;
  //   Stop_Execution = Continue_Execution; Invalid_Instr = Valid_Instr

  // Notes on the sheet:
  //   Microcode
  //   contents of rom_1 (hex, n*v repeats v):
  //   96*600000 4*805 4*825 4*865 4*600000 4*80d 4*82d 488*600000 4*803 b03 600000 600000 600000 4*c83
  //   4*d03 4*e83 b83 600000 c03 600000 4*d83 4*e03 96*600000 32*100803 352*600000 16*40810 496*600000 3
  //   103 83 600000 303 183 600000 600000 483 600000 600000 600000 503 600000 600000 600000 683 203 600000
  //   600000 383 600000 403 600000 583 283 600000 600000 603 99*600000 32*100f03 1376*600000 4*93800
  //   4*9b800 8*600000 4*83800 4*8b800 4*a3800 4*ab800 96*600000 4*4801 252*600000 32*c5801 96*600000
  //   200000 415*600000
endmodule

module RAM (
  input  [31:0] ALU,
  input  [31:0] Write_Data,
  input  clk,
  input  clr,
  input  Wr_En,
  input  [1:0] RAM_num,
  input  Read_Unsigned,
  output [31:0] RAM_Out
);

  wire [7:0] b0_out, b1_out, b2_out, b3_out;
  wire [22:0] H110;
  wire [31:0] extend_byte_s_1_out, extend_byte_s_2_out, extend_byte_s_3_out, extend_byte_s_4_out,
       extend_byte_u_1_out, extend_byte_u_2_out, extend_byte_u_3_out, extend_byte_u_4_out,
       extend_half_s_1_out, extend_half_s_2_out, extend_half_s_3_out, extend_half_s_4_out,
       extend_half_u_1_out, extend_half_u_2_out, extend_half_u_3_out, extend_half_u_4_out,
       extend_tronple_s_1_out, extend_tronple_s_2_out, extend_tronple_s_3_out, extend_tronple_s_4_out,
       extend_tronple_u_1_out, extend_tronple_u_2_out, extend_tronple_u_3_out, extend_tronple_u_4_out,
       multiplexer_1_out, multiplexer_2_out, multiplexer_3_out, multiplexer_4_out;

  Adder #(.width(23)) adder_1 (.a(ALU[24:2]), .b(23'h1), .out(H110));  // open: cin, cout
  Multiplexer #(.select(4), .width(32), .enable("false")) multiplexer_1 (
    .in0({Wr_En, Write_Data[7:0], ALU[24:2]}), .in1({32{1'b0}}), .in2({32{1'b0}}), .in3({32{1'b0}}),
    .in4({Wr_En, Write_Data[7:0], ALU[24:2]}), .in5({32{1'b0}}), .in6({32{1'b0}}),
    .in7({Wr_En, Write_Data[15:8], H110}), .in8({Wr_En, Write_Data[7:0], ALU[24:2]}), .in9({32{1'b0}}),
    .in10({Wr_En, Write_Data[23:16], H110}), .in11({Wr_En, Write_Data[15:8], H110}),
    .in12({Wr_En, Write_Data[7:0], ALU[24:2]}), .in13({Wr_En, Write_Data[31:24], H110}),
    .in14({Wr_En, Write_Data[23:16], H110}), .in15({Wr_En, Write_Data[15:8], H110}), .out(multiplexer_1_out),
    .sel({RAM_num, ALU[1:0]}));
  Multiplexer #(.select(4), .width(32), .enable("false")) multiplexer_2 (
    .in0({32{1'b0}}), .in1({Wr_En, Write_Data[7:0], ALU[24:2]}), .in2({32{1'b0}}), .in3({32{1'b0}}),
    .in4({Wr_En, Write_Data[15:8], ALU[24:2]}), .in5({Wr_En, Write_Data[7:0], ALU[24:2]}), .in6({32{1'b0}}),
    .in7({32{1'b0}}), .in8({Wr_En, Write_Data[15:8], ALU[24:2]}), .in9({Wr_En, Write_Data[7:0], ALU[24:2]}),
    .in10({32{1'b0}}), .in11({Wr_En, Write_Data[23:16], H110}), .in12({Wr_En, Write_Data[15:8], ALU[24:2]}),
    .in13({Wr_En, Write_Data[7:0], ALU[24:2]}), .in14({Wr_En, Write_Data[31:24], H110}),
    .in15({Wr_En, Write_Data[23:16], H110}), .out(multiplexer_2_out), .sel({RAM_num, ALU[1:0]}));
  Multiplexer #(.select(4), .width(32), .enable("false")) multiplexer_3 (
    .in0({32{1'b0}}), .in1({32{1'b0}}), .in2({Wr_En, Write_Data[7:0], ALU[24:2]}), .in3({32{1'b0}}),
    .in4({32{1'b0}}), .in5({Wr_En, Write_Data[15:8], ALU[24:2]}), .in6({Wr_En, Write_Data[7:0], ALU[24:2]}),
    .in7({32{1'b0}}), .in8({Wr_En, Write_Data[23:16], ALU[24:2]}),
    .in9({Wr_En, Write_Data[15:8], ALU[24:2]}), .in10({Wr_En, Write_Data[7:0], ALU[24:2]}),
    .in11({32{1'b0}}), .in12({Wr_En, Write_Data[23:16], ALU[24:2]}),
    .in13({Wr_En, Write_Data[15:8], ALU[24:2]}), .in14({Wr_En, Write_Data[7:0], ALU[24:2]}),
    .in15({Wr_En, Write_Data[31:24], H110}), .out(multiplexer_3_out), .sel({RAM_num, ALU[1:0]}));
  Multiplexer #(.select(4), .width(32), .enable("false")) multiplexer_4 (
    .in0({32{1'b0}}), .in1({32{1'b0}}), .in2({32{1'b0}}), .in3({Wr_En, Write_Data[7:0], ALU[24:2]}),
    .in4({32{1'b0}}), .in5({32{1'b0}}), .in6({Wr_En, Write_Data[15:8], ALU[24:2]}),
    .in7({Wr_En, Write_Data[7:0], ALU[24:2]}), .in8({32{1'b0}}), .in9({Wr_En, Write_Data[23:16], ALU[24:2]}),
    .in10({Wr_En, Write_Data[15:8], ALU[24:2]}), .in11({Wr_En, Write_Data[7:0], ALU[24:2]}),
    .in12({Wr_En, Write_Data[31:24], ALU[24:2]}), .in13({Wr_En, Write_Data[23:16], ALU[24:2]}),
    .in14({Wr_En, Write_Data[15:8], ALU[24:2]}), .in15({Wr_En, Write_Data[7:0], ALU[24:2]}),
    .out(multiplexer_4_out), .sel({RAM_num, ALU[1:0]}));
  RAM_part #(.addrWidth(23), .bus("separate")) ram_1 (
    .addr(multiplexer_1_out[22:0]), .din(multiplexer_1_out[30:23]), .data(b0_out),
    .str(multiplexer_1_out[31]), .clk(clk), .clr(clr));  // open: sel, ld
  RAM_part #(.addrWidth(23), .bus("separate")) ram_2 (
    .addr(multiplexer_2_out[22:0]), .din(multiplexer_2_out[30:23]), .data(b1_out),
    .str(multiplexer_2_out[31]), .clk(clk), .clr(clr));  // open: sel, ld
  RAM_part #(.addrWidth(23), .bus("separate")) ram_3 (
    .addr(multiplexer_3_out[22:0]), .din(multiplexer_3_out[30:23]), .data(b2_out),
    .str(multiplexer_3_out[31]), .clk(clk), .clr(clr));  // open: sel, ld
  RAM_part #(.addrWidth(23), .bus("separate")) ram_4 (
    .addr(multiplexer_4_out[22:0]), .din(multiplexer_4_out[30:23]), .data(b3_out),
    .str(multiplexer_4_out[31]), .clk(clk), .clr(clr));  // open: sel, ld
  Extend_Byte_S extend_byte_s_1 (.In(b0_out), .Out(extend_byte_s_1_out));
  Extend_Byte_U extend_byte_u_1 (.In(b0_out), .Out(extend_byte_u_1_out));
  Extend_Byte_S extend_byte_s_2 (.In(b1_out), .Out(extend_byte_s_2_out));
  Extend_Byte_U extend_byte_u_2 (.In(b1_out), .Out(extend_byte_u_2_out));
  Extend_Byte_S extend_byte_s_3 (.In(b2_out), .Out(extend_byte_s_3_out));
  Extend_Byte_U extend_byte_u_3 (.In(b2_out), .Out(extend_byte_u_3_out));
  Extend_Byte_S extend_byte_s_4 (.In(b3_out), .Out(extend_byte_s_4_out));
  Extend_Byte_U extend_byte_u_4 (.In(b3_out), .Out(extend_byte_u_4_out));
  Extend_Half_S extend_half_s_1 (.In({b1_out, b0_out}), .Out(extend_half_s_1_out));
  Extend_Half_U extend_half_u_1 (.In({b1_out, b0_out}), .Out(extend_half_u_1_out));
  Extend_Half_S extend_half_s_2 (.In({b2_out, b1_out}), .Out(extend_half_s_2_out));
  Extend_Half_U extend_half_u_2 (.In({b2_out, b1_out}), .Out(extend_half_u_2_out));
  Extend_Half_S extend_half_s_3 (.In({b3_out, b2_out}), .Out(extend_half_s_3_out));
  Extend_Half_U extend_half_u_3 (.In({b3_out, b2_out}), .Out(extend_half_u_3_out));
  Extend_Half_S extend_half_s_4 (.In({b0_out, b3_out}), .Out(extend_half_s_4_out));
  Extend_Half_U extend_half_u_4 (.In({b0_out, b3_out}), .Out(extend_half_u_4_out));
  Extend_Tronple_S extend_tronple_s_1 (.In({b2_out, b1_out, b0_out}), .Out(extend_tronple_s_1_out));
  Extend_Tronple_U extend_tronple_u_1 (.In({b2_out, b1_out, b0_out}), .Out(extend_tronple_u_1_out));
  Extend_Tronple_S extend_tronple_s_2 (.In({b3_out, b2_out, b1_out}), .Out(extend_tronple_s_2_out));
  Extend_Tronple_U extend_tronple_u_2 (.In({b3_out, b2_out, b1_out}), .Out(extend_tronple_u_2_out));
  Extend_Tronple_S extend_tronple_s_3 (.In({b0_out, b3_out, b2_out}), .Out(extend_tronple_s_3_out));
  Extend_Tronple_U extend_tronple_u_3 (.In({b0_out, b3_out, b2_out}), .Out(extend_tronple_u_3_out));
  Extend_Tronple_S extend_tronple_s_4 (.In({b1_out, b0_out, b3_out}), .Out(extend_tronple_s_4_out));
  Extend_Tronple_U extend_tronple_u_4 (.In({b1_out, b0_out, b3_out}), .Out(extend_tronple_u_4_out));
  Multiplexer #(.select(5), .width(32), .enable("false")) multiplexer_5 (
    .in0(extend_byte_s_1_out), .in1(extend_byte_u_1_out), .in2(extend_byte_s_2_out),
    .in3(extend_byte_u_2_out), .in4(extend_byte_s_3_out), .in5(extend_byte_u_3_out),
    .in6(extend_byte_s_4_out), .in7(extend_byte_u_4_out), .in8(extend_half_s_1_out),
    .in9(extend_half_u_1_out), .in10(extend_half_s_2_out), .in11(extend_half_u_2_out),
    .in12(extend_half_s_3_out), .in13(extend_half_u_3_out), .in14(extend_half_s_4_out),
    .in15(extend_half_u_4_out), .in16(extend_tronple_s_1_out), .in17(extend_tronple_u_1_out),
    .in18(extend_tronple_s_2_out), .in19(extend_tronple_u_2_out), .in20(extend_tronple_s_3_out),
    .in21(extend_tronple_u_3_out), .in22(extend_tronple_s_4_out), .in23(extend_tronple_u_4_out),
    .in24({b3_out, b2_out, b1_out, b0_out}), .in25({b3_out, b2_out, b1_out, b0_out}),
    .in26({b0_out, b3_out, b2_out, b1_out}), .in27({b0_out, b3_out, b2_out, b1_out}),
    .in28({b1_out, b0_out, b3_out, b2_out}), .in29({b1_out, b0_out, b3_out, b2_out}),
    .in30({b2_out, b1_out, b0_out, b3_out}), .in31({b2_out, b1_out, b0_out, b3_out}), .out(RAM_Out),
    .sel({RAM_num, ALU[1:0], Read_Unsigned}));

  // Other names for the same wires on the sheet: Byte_Index[1:0] = ALU[1:0]; Encoding[3:0] = {RAM_num, ALU[1:0]};
  //   b1[7:0] = Write_Data[15:8]; H001[31:0] = {Wr_En, Write_Data[15:8], ALU[24:2]};
  //   H012[31:0] = {Wr_En, Write_Data[15:8], ALU[24:2]}; H103[31:0] = {Wr_En, Write_Data[15:8], ALU[24:2]};
  //   H110[31:23] = {Wr_En, Write_Data[15:8]}; T001[31:0] = {Wr_En, Write_Data[15:8], ALU[24:2]};
  //   T012[31:0] = {Wr_En, Write_Data[15:8], ALU[24:2]}; T103[31:0] = {Wr_En, Write_Data[15:8], ALU[24:2]};
  //   T110[31:0] = {Wr_En, Write_Data[15:8], H110}; W001[31:0] = {Wr_En, Write_Data[15:8], ALU[24:2]};
  //   W012[31:0] = {Wr_En, Write_Data[15:8], ALU[24:2]}; W103[31:0] = {Wr_En, Write_Data[15:8], ALU[24:2]};
  //   W110[31:0] = {Wr_En, Write_Data[15:8], H110}; b2[7:0] = Write_Data[23:16];
  //   T002[31:0] = {Wr_En, Write_Data[23:16], ALU[24:2]}; T013[31:0] = {Wr_En, Write_Data[23:16], ALU[24:2]};
  //   T100[31:0] = {Wr_En, Write_Data[23:16], H110}; T111[31:0] = {Wr_En, Write_Data[23:16], H110};
  //   W002[31:0] = {Wr_En, Write_Data[23:16], ALU[24:2]}; W013[31:0] = {Wr_En, Write_Data[23:16], ALU[24:2]};
  //   W100[31:0] = {Wr_En, Write_Data[23:16], H110}; W111[31:0] = {Wr_En, Write_Data[23:16], H110};
  //   W010[31:0] = {Wr_En, Write_Data[31:24], H110}; W101[31:0] = {Wr_En, Write_Data[31:24], H110};
  //   W112[31:0] = {Wr_En, Write_Data[31:24], H110}; Word_Align___1[22:0] = H110; b3[7:0] = Write_Data[31:24];
  //   W003[31:0] = {Wr_En, Write_Data[31:24], ALU[24:2]}; B000[31:0] = {Wr_En, Write_Data[7:0], ALU[24:2]};
  //   B011[31:0] = {Wr_En, Write_Data[7:0], ALU[24:2]}; B102[31:0] = {Wr_En, Write_Data[7:0], ALU[24:2]};
  //   B113[31:0] = {Wr_En, Write_Data[7:0], ALU[24:2]}; H000[31:0] = {Wr_En, Write_Data[7:0], ALU[24:2]};
  //   H011[31:0] = {Wr_En, Write_Data[7:0], ALU[24:2]}; H102[31:0] = {Wr_En, Write_Data[7:0], ALU[24:2]};
  //   H113[31:0] = {Wr_En, Write_Data[7:0], ALU[24:2]}; T000[31:0] = {Wr_En, Write_Data[7:0], ALU[24:2]};
  //   T011[31:0] = {Wr_En, Write_Data[7:0], ALU[24:2]}; T102[31:0] = {Wr_En, Write_Data[7:0], ALU[24:2]};
  //   T113[31:0] = {Wr_En, Write_Data[7:0], ALU[24:2]}; W000[31:0] = {Wr_En, Write_Data[7:0], ALU[24:2]};
  //   W011[31:0] = {Wr_En, Write_Data[7:0], ALU[24:2]}; W102[31:0] = {Wr_En, Write_Data[7:0], ALU[24:2]};
  //   W113[31:0] = {Wr_En, Write_Data[7:0], ALU[24:2]}; Word_Align[22:0] = ALU[24:2]; b0[7:0] = Write_Data[7:0];
  //   wen = Wr_En

  // Notes on the sheet:
  //    (00) Byte
  //   (01) Half
  //   (10) Tronple
  //   (11) Word
  //   0
  //   1
  //   2
  //   3
  //   0
  //   1
  //   2
  //   3
  //   0
  //   1
  //   2
  //   3
  //   0
  //   1
  //   2
  //   3
  //   00
  //   0
  //   1
  //   2
  //   3
  //   0
  //   1
  //   2
  //   3
  //   0
  //   1
  //   2
  //   3
  //   0
  //   1
  //   2
  //   3
  //   01
  //   Encoding = RAM# | Byte Index
  //   0
  //   1
  //   2
  //   3
  //   0
  //   1
  //   2
  //   3
  //   0
  //   1
  //   2
  //   3
  //   0
  //   1
  //   2
  //   3
  //   10
  //   0
  //   1
  //   2
  //   3
  //   0
  //   1
  //   2
  //   3
  //   0
  //   1
  //   2
  //   3
  //   0
  //   1
  //   2
  //   3
  //   11
  //   Byte 0
  //   Byte 1
  //   Byte 2
  //   Byte 3
endmodule

module Extend_Byte_S (
  input  [7:0] In,
  output [31:0] Out
);

  assign Out = {{24{In[7]}}, In};  // Bit_Extender bit_extender_1
endmodule

module Extend_Byte_U (
  input  [7:0] In,
  output [31:0] Out
);

  assign Out = {{24{1'b0}}, In};  // Bit_Extender bit_extender_1
endmodule

module Extend_Half_S (
  input  [15:0] In,
  output [31:0] Out
);

  assign Out = {{16{In[15]}}, In};  // Bit_Extender bit_extender_1
endmodule

module Extend_Half_U (
  input  [15:0] In,
  output [31:0] Out
);

  assign Out = {{16{1'b0}}, In};  // Bit_Extender bit_extender_1
endmodule

module Extend_Tronple_S (
  input  [23:0] In,
  output [31:0] Out
);

  assign Out = {{8{In[23]}}, In};  // Bit_Extender bit_extender_1
endmodule

module Extend_Tronple_U (
  input  [23:0] In,
  output [31:0] Out
);

  assign Out = {{8{1'b0}}, In};  // Bit_Extender bit_extender_1
endmodule
